# Fritzing sketch main (saved by Fritzing 0.9.4)

parts:
  SW1 = Rotary_encoder [package=encoder_led_3]
  SW2 = Rotary_encoder [package=encoder_led_3]
  SW3 = Rotary_encoder [package=encoder_led_3]
  U4 = Slide_potentiometer_10k [package=slider]
  U5 = Slide_potentiometer_10k [package=slider]
  U6 = Slide_potentiometer_10k [package=slider]
  Pro_Micro1 = SparkFun Pro Micro
  S1 = Round Pushbutton
  S2 = Round Pushbutton
  S3 = Round Pushbutton
  S4 = Round Pushbutton
  S5 = Round Pushbutton
  S6 = Round Pushbutton
  S7 = Round Pushbutton
  S8 = Round Pushbutton
  S9 = Round Pushbutton
  S10 = Round Pushbutton
  S11 = Round Pushbutton
  S12 = Round Pushbutton
  S13 = Round Pushbutton
  S14 = Round Pushbutton
  S15 = Round Pushbutton
  S16 = Round Pushbutton
  Part1 = Analog Digital MUX Breakout

nets:
  N1: SW1.CLK, Pro_Micro1.9
  N2: SW1.DT, Pro_Micro1.8
  N3: SW1.SW, Pro_Micro1.7
  VCC: SW1.+, SW2.+, SW3.+, U4.VCC, U5.VCC, U6.VCC, Pro_Micro1.VCC, Part1.VCC
  GND: SW1.GND, SW2.GND, SW3.GND, U4.GND, U5.GND, U6.GND, Pro_Micro1.GND, S1.leg1, Part1.GND, Part1.EN
  N4: SW2.CLK, Pro_Micro1.6
  N5: SW2.SW, Pro_Micro1.5
  N6: SW3.CLK, Pro_Micro1.3
  N7: SW3.DT, Pro_Micro1.2
  N8: SW3.SW, Pro_Micro1.RX1
  N9: U4.OTB, Pro_Micro1.A0
  N10: U5.OTB, Pro_Micro1.A1
  N11: U6.OTB, Pro_Micro1.A2
  N12: Pro_Micro1.10, Part1.S0
  N13: Pro_Micro1.16, Part1.S1
  N14: Pro_Micro1.14, Part1.S2
  N15: Pro_Micro1.15, Part1.S3
  N16: Pro_Micro1.A3, Part1.SIG
  N17: S1.leg0, Part1.C0
  N18: S2.leg0, Part1.C1
  N19: S3.leg0, Part1.C2
  N20: S4.leg0, Part1.C4
  N21: S5.leg0, Part1.C5
  N22: S6.leg0, Part1.C6
  N23: S7.leg0, Part1.C3
  N24: S8.leg0, Part1.C7
  N25: S9.leg0, Part1.C8
  N26: S10.leg0, Part1.C11
  N27: S11.leg0, Part1.C10
  N28: S12.leg0, Part1.C9
  N29: S13.leg0, Part1.C12
  N30: S14.leg0, Part1.C15
  N31: S15.leg0, Part1.C14
  N32: S16.leg0, Part1.C13

custom parts:
  Rotary_encoder: 360 Degrees Rotary Encoder Module For Arduino
  Slide_potentiometer_10k: Slide Potentiometer 10K Linear Module Dual Output for Arduino AVR Electronic Block
  SparkFun Pro Micro: The Pro Micro is similar to the Pro Mini except with an ATmega32U4 on board. The USB transceiver inside the 32U4 allows us to add USB connectivity on-board and do away with bulky external USB interface. Based on: https://github.com/unorthodox-engineers/unorthodox-arduino/blob/master/Unorthodox/fritzing/parts/Pro%20Micro.fzpz
